# Fritzing sketch arduinoCircuit (saved by Fritzing 0.9.3b)
breadboards: 1

parts:
  Componente1 = Arduino Nano (Rev3.0)
  R1 = Resistor [tolerance=±5% resistance=220 package=THT]
  R2 = Photocell (LDR) [package=THT]
  Componente2 = Bluetooth HC-05 Macho
  J1 = Basic Servo

nets:
  GND: Componente1.GND, R2.pin_1, Componente2.GND, J1.gnd
  N1: Componente1.D3, J1.pulse
  N2: Componente1.D7, Componente2.TXD
  N3: Componente1.D8, Componente2.RXD
  VCC: Componente1.5V, R1.Pin_0, Componente2.VCC, J1.vcc
  N4: Componente1.A0, R1.Pin_1, R2.pin_0
